# Fritzing sketch StoplightSketch (saved by Fritzing 0.9.2b)
breadboards: 1

parts:
  Part1 = Arduino Uno (Rev3)
  LED1 = LED - 5mm [color="Red (633nm)" package="5 mm [THT]"]
  R1 = Resistor [tolerance=±5% resistance=220 package=THT]
  LED2 = LED - 5mm [color="Yellow (585nm)" package="5 mm [THT]"]
  R2 = Resistor [tolerance=±5% resistance=220 package=THT]
  LED3 = LED - 5mm [color="Green (565nm)" package="5 mm [THT]"]
  R3 = Resistor [tolerance=±5% resistance=220 package=THT]
  LED4 = LED - 5mm [color="Green (570nm)" package="5 mm [THT]"]
  R4 = Resistor [tolerance=±5% resistance=220 package=THT]
  LED5 = LED - 5mm [color="Orange (612nm)" package="5 mm [THT]"]
  R5 = Resistor [tolerance=±5% resistance=220 package=THT]
  S1 = Pushbutton [package="[THT]"]
  S2 = Pushbutton [package="[THT]"]
  R6 = Resistor [tolerance=±5% resistance=220 package=THT]
  R7 = Resistor [tolerance=±5% resistance=220 package=THT]
  R8 = Photocell (LDR) [package=THT]
  R9 = Resistor [tolerance=±5% resistance=220 package=THT]

nets:
  N1: Part1.A0, R8.pin_1, R9.Pin_1
  N2: Part1.A1, LED5.anode, R5.Pin_1
  N3: Part1.D10_PWM/SS, LED4.anode
  N4: Part1.D11_PWM/MOSI, LED3.anode
  N5: Part1.D12/MISO, LED2.anode
  N6: Part1.D13/SCK, LED1.anode
  N7: Part1.GND, R1.Pin_1, R2.Pin_1, R3.Pin_1, R4.Pin_1, LED5.cathode, R6.Pin_0, R7.Pin_0, R9.Pin_0
  N8: Part1.D5_PWM, R5.Pin_0
  N9: Part1.D6_PWM, S2.Pin_1, S2.Pin_2, R7.Pin_1
  N10: Part1.D7, S1.Pin_1, S1.Pin_2, R6.Pin_1
  N11: Part1.5V, S1.Pin_3, S1.Pin_4, S2.Pin_4, R8.pin_0
  N12: LED1.cathode, R1.Pin_0
  N13: LED2.cathode, R2.Pin_0
  N14: LED3.cathode, R3.Pin_0
  N15: LED4.cathode, R4.Pin_0
